# Fritzing sketch watering_system (saved by Fritzing 0.9.3b)
breadboards: 1

parts:
  Chirp!_Soil_Moisture_Sensor1 = Chirp! Soil Moisture Sensor v2.7.3
  U1 = NodeMCU V3.0
  KY-1 = Keyes Relay [package=THT]
  BAT1 = BC9VPC [package=bc9vpc]

nets:
  N1: Chirp!_Soil_Moisture_Sensor1.Pin_1, U1.Vin
  N2: Chirp!_Soil_Moisture_Sensor1.pin_3, U1.A0
  N3: Chirp!_Soil_Moisture_Sensor1.pin_5, U1.GND#6, U1.GND#13, U1.GND#16, U1.GND#33, KY-1.ground
  N4: U1.D3, KY-1.signal
  N5: U1.3V3, KY-1.power
  N6: KY-1.C, BAT1.V+

notes:
  (+) Water Pump (-)

custom parts:
  NodeMCU V3.0: ESP8266 based NodeMCU
  Keyes Relay: The Keyes 5V relay module is suitable for SCM development, home appliance control. It uses a 5V~12V TIL control signal which can control DC / AC signal.
